// Logisim project final_computer.circ as structural Verilog: 9 circuits, main circuit Computer
module Computer (
  input  in_1
);

  wire clock_1_out, clock_2_out, clock_3_out, keyboard_1_avail, keyboardcontroller_1_keyboardread,
       keyboardcontroller_1_writetobus, memorycontroller_1_writeenabletomem, memorycontroller_1_writetobus,
       new_cpu_1_buswriteenable, rgb_video_1_p4, rgb_video_1_p5, terminalcontroller_1_writetoterminal;
  wire [6:0] keyboard_1_data, terminalcontroller_1_datatoterminal;
  wire [7:0] rgb_video_1_p6, rgb_video_1_p7;
  wire [23:0] memorycontroller_1_addresstomem, rgb_video_1_p8;
  wire [25:0] new_cpu_1_addresstobus;
  wire [31:0] controlled_buffer_1_out, keyboardcontroller_1_datatobus, memorycontroller_1_datatobus,
       memorycontroller_1_datatomem, new_cpu_1_datatobus, ram_1_dout;

  RAM #(.addrWidth(24), .dataWidth(32), .enables("line")) ram_1 (
    .addr(memorycontroller_1_addresstomem), .we(memorycontroller_1_writeenabletomem), .clk(clock_1_out),
    .din(memorycontroller_1_datatomem), .dout(ram_1_dout));
  Clock clock_1 (.out(clock_1_out));
  Clock clock_2 (.out(clock_2_out));
  Keyboard keyboard_1 (
    .clk(clock_2_out), .re(keyboardcontroller_1_keyboardread), .avail(keyboard_1_avail),
    .data(keyboard_1_data));  // open: clr
  MemoryController memorycontroller_1 (
    .WriteEnableFromBus(new_cpu_1_buswriteenable), .AddressFromBus(new_cpu_1_addresstobus),
    .DataFromBus(controlled_buffer_1_out), .DataFromMem(ram_1_dout),
    .WriteEnableToMem(memorycontroller_1_writeenabletomem), .DataToBus(memorycontroller_1_datatobus),
    .AddressToMem(memorycontroller_1_addresstomem), .DataToMem(memorycontroller_1_datatomem),
    .WriteToBus(memorycontroller_1_writetobus));
  NEW_CPU new_cpu_1 (
    .in_1(controlled_buffer_1_out), .DataToBus(new_cpu_1_datatobus), .AddressToBus(new_cpu_1_addresstobus),
    .BusWriteEnable(new_cpu_1_buswriteenable));  // open: WE_MEM
  assign controlled_buffer_1_out = memorycontroller_1_writetobus ? memorycontroller_1_datatobus : 32'bz;  // Controlled_Buffer controlled_buffer_1
  assign controlled_buffer_1_out = new_cpu_1_buswriteenable ? new_cpu_1_datatobus : 32'bz;  // Controlled_Buffer controlled_buffer_2
  KeyboardController keyboardcontroller_1 (
    .DataFromBus(controlled_buffer_1_out), .WriteEnableFromBus(new_cpu_1_buswriteenable),
    .AddressFromBus(new_cpu_1_addresstobus), .KeyboardData(keyboard_1_data),
    .KeyboardStatus(keyboard_1_avail), .KeyboardRead(keyboardcontroller_1_keyboardread),
    .WriteToBus(keyboardcontroller_1_writetobus), .DataToBus(keyboardcontroller_1_datatobus));
  assign controlled_buffer_1_out = keyboardcontroller_1_writetobus ? keyboardcontroller_1_datatobus : 32'bz;  // Controlled_Buffer controlled_buffer_3
  Clock clock_3 (.out(clock_3_out));
  TTY tty_1 (
    .data(terminalcontroller_1_datatoterminal), .clk(clock_3_out), .we(terminalcontroller_1_writetoterminal),
    .clr(in_1));
  // RGB_Video #(.height(256), .scale(1), .width(256)) rgb_video_1: pin names not known; wires that end beside it: controlled_buffer_1_out, new_cpu_1_addresstobus, new_cpu_1_buswriteenable, rgb_video_1_p4, rgb_video_1_p5, rgb_video_1_p6, rgb_video_1_p7, rgb_video_1_p8
  Clock clock_4 (.out(rgb_video_1_p4));
  TerminalController terminalcontroller_1 (
    .WriteEnableFromBus(new_cpu_1_buswriteenable), .AddressFromBus(new_cpu_1_addresstobus),
    .DataFromBus(controlled_buffer_1_out), .DataToTerminal(terminalcontroller_1_datatoterminal),
    .WriteToTerminal(terminalcontroller_1_writetoterminal));
  RGBController rgbcontroller_1 (
    .AddressFromBus(new_cpu_1_addresstobus), .DataFromBus(controlled_buffer_1_out),
    .WriteEnable(new_cpu_1_buswriteenable), .RGBX(rgb_video_1_p6), .RGBY(rgb_video_1_p7),
    .RGBColor(rgb_video_1_p8), .RGBWrite(rgb_video_1_p5));

  // Notes on the sheet:
  //   Write_enable
  //   Address
  //   Data
endmodule

module NEW_CPU (
  input  [31:0] in_1,
  output [31:0] DataToBus,
  output [25:0] AddressToBus,
  output BusWriteEnable,
  output WE_MEM
);

  wire and_1_out, and_2_out, clock_1_out, comparator_1_eq, comparator_2_eq, comparator_3_eq, comparator_4_eq,
       comparator_5_eq, comparator_6_eq, comparator_7_eq, comparator_8_eq, comparator_9_eq, new_alu_1_equal,
       new_control_1_aluvmemselect, new_control_1_imm_sel, new_control_1_we_regfile, not_1_out, or_1_out,
       or_2_out, or_3_out, or_4_out, or_5_out, or_6_out;
  wire [4:0] new_control_1_alu_operation, new_control_1_rd_select, new_control_1_rs_select,
       new_control_1_rt_select, new_control_1_shamt;
  wire [15:0] bit_extender_3_out, shifter_1_out;
  wire [25:0] bit_extender_4_out, shifter_2_out;
  wire [31:0] adder_1_out, bit_extender_1_out, bit_extender_2_out, bit_extender_5_out, multiplexer_1_out,
       multiplexer_2_out, multiplexer_3_out, multiplexer_4_out, multiplexer_5_out, multiplexer_6_out,
       multiplexer_7_out, new_alu_1_res, new_control_1_imm, new_regfile_1_rs_data, ProgramCounter_q,
       rom_1_data, shifter_3_out, shifter_4_out;

  Adder #(.width(32)) adder_1 (.a(ProgramCounter_q), .b(32'h4), .out(adder_1_out));  // open: cin, cout
  assign bit_extender_1_out = {{16{shifter_1_out[15]}}, shifter_1_out};  // Bit_Extender bit_extender_1
  Shifter #(.width(16)) shifter_1 (.in(new_control_1_imm[15:0]), .\dist (4'b0010), .out(shifter_1_out));
  Shifter #(.width(26)) shifter_2 (.in(bit_extender_4_out), .\dist (5'b00010), .out(shifter_2_out));
  Multiplexer #(.width(32)) multiplexer_1 (
    .in0(adder_1_out), .in1(bit_extender_1_out), .out(multiplexer_1_out), .sel(or_6_out));
  assign bit_extender_2_out = {{6{shifter_2_out[25]}}, shifter_2_out};  // Bit_Extender bit_extender_2
  Multiplexer #(.width(32)) multiplexer_2 (
    .in0(bit_extender_2_out), .in1(new_regfile_1_rs_data), .out(multiplexer_2_out), .sel(or_5_out));
  Shifter #(.shift("lr"), .width(32)) shifter_3 (.in(ProgramCounter_q), .\dist (5'b00010), .out(shifter_3_out));
  Register #(.width(32)) ProgramCounter (
    .D(multiplexer_3_out), .en(1'b1), .clk(clock_1_out), .Q(ProgramCounter_q));  // open: clr
  Multiplexer #(.width(32)) multiplexer_3 (
    .in0(multiplexer_1_out), .in1(multiplexer_2_out), .out(multiplexer_3_out), .sel(or_3_out));
  Clock clock_1 (.out(clock_1_out));
  ROM #(.addrWidth(16), .dataWidth(32)) rom_1 (.addr(bit_extender_3_out), .data(rom_1_data));
  Bit_Extender #(.in_width(32)) bit_extender_3 (.in(shifter_3_out), .out(bit_extender_3_out));
  Bit_Extender #(.in_width(32), .out_width(26)) bit_extender_4 (.in(rom_1_data), .out(bit_extender_4_out));
  // Probe on rom_1_data
  Multiplexer #(.width(32)) multiplexer_4 (
    .in0(new_alu_1_res), .in1(in_1), .out(multiplexer_4_out), .sel(new_control_1_aluvmemselect));
  Multiplexer #(.width(32)) multiplexer_5 (
    .in0(multiplexer_4_out), .in1(adder_1_out), .out(multiplexer_5_out), .sel(or_1_out));
  NEW_Control new_control_1 (
    .Inst(rom_1_data), .imm(new_control_1_imm), .imm_sel(new_control_1_imm_sel),
    .we_regfile(new_control_1_we_regfile), .rs_select(new_control_1_rs_select),
    .rt_select(new_control_1_rt_select), .rd_select(new_control_1_rd_select),
    .ALU_operation(new_control_1_alu_operation), .ALUvMEMselect(new_control_1_aluvmemselect),
    .we_mem(WE_MEM), .Shamt(new_control_1_shamt));
  NEW_regfile new_regfile_1 (
    .RS_Select(new_control_1_rs_select), .RT_Select(new_control_1_rt_select),
    .Write_Enable(new_control_1_we_regfile), .RD_Select(new_control_1_rd_select),
    .RD_Data(multiplexer_5_out), .RS_Data(new_regfile_1_rs_data), .RT_Data(DataToBus));
  Comparator #(.mode("unsigned"), .width(5)) comparator_1 (
    .a(new_control_1_alu_operation), .b(5'b10001), .eq(comparator_1_eq));  // open: gt, lt
  Comparator #(.mode("unsigned"), .width(5)) comparator_2 (
    .a(new_control_1_alu_operation), .b(5'b10011), .eq(comparator_2_eq));  // open: gt, lt
  // Probe on new_control_1_alu_operation
  or or_1 (or_1_out, comparator_1_eq, comparator_2_eq);
  Comparator #(.width(5)) comparator_3 (
    .a(new_control_1_alu_operation), .b(5'b00110), .eq(comparator_3_eq));  // open: gt, lt
  Comparator #(.width(5)) comparator_4 (
    .a(new_control_1_alu_operation), .b(5'b00101), .eq(comparator_4_eq));  // open: gt, lt
  or or_2 (or_2_out, comparator_5_eq, comparator_3_eq, comparator_4_eq);
  Comparator #(.width(5)) comparator_5 (
    .a(new_control_1_alu_operation), .b(5'b01000), .eq(comparator_5_eq));  // open: gt, lt
  Multiplexer #(.width(32)) multiplexer_6 (
    .in0(new_regfile_1_rs_data), .in1(DataToBus), .out(multiplexer_6_out), .sel(or_2_out));
  assign bit_extender_5_out = {{16{new_control_1_imm[15]}}, new_control_1_imm[15:0]};  // Bit_Extender bit_extender_5
  Multiplexer #(.width(32)) multiplexer_7 (
    .in0(DataToBus), .in1(bit_extender_5_out), .out(multiplexer_7_out), .sel(new_control_1_imm_sel));
  Comparator #(.mode("unsigned"), .width(5)) comparator_6 (
    .a(new_control_1_alu_operation), .b(5'b01111), .eq(comparator_6_eq));  // open: gt, lt
  Comparator #(.mode("unsigned"), .width(5)) comparator_7 (
    .a(new_control_1_alu_operation), .b(5'b10000), .eq(comparator_7_eq));  // open: gt, lt
  or or_3 (or_3_out, or_1_out, or_4_out);
  or or_4 (or_4_out, comparator_6_eq, comparator_7_eq);
  or or_5 (or_5_out, comparator_7_eq, comparator_2_eq);
  // Probe on DataToBus
  NEW_ALU new_alu_1 (
    .OP1(multiplexer_6_out), .OP2(multiplexer_7_out), .shift(new_control_1_shamt),
    .ALU_CODE(new_control_1_alu_operation), .Res(new_alu_1_res), .equal(new_alu_1_equal));
  Comparator #(.mode("unsigned"), .width(5)) comparator_8 (
    .a(new_control_1_alu_operation), .b(5'b01010), .eq(comparator_8_eq));  // open: gt, lt
  Comparator #(.mode("unsigned"), .width(5)) comparator_9 (
    .a(new_control_1_alu_operation), .b(5'b01011), .eq(comparator_9_eq));  // open: gt, lt
  not not_1 (not_1_out, new_alu_1_equal);
  Bit_Extender #(.in_width(32), .out_width(26)) bit_extender_6 (.in(shifter_4_out), .out(AddressToBus));
  Shifter #(.shift("lr"), .width(32)) shifter_4 (.in(new_alu_1_res), .\dist (5'b00010), .out(shifter_4_out));
  and and_1 (and_1_out, comparator_8_eq, new_alu_1_equal);
  and and_2 (and_2_out, comparator_9_eq, not_1_out);
  Clock clock_2 ();  // open: out
  Comparator #(.width(5)) comparator_10 (
    .a(new_control_1_alu_operation), .b(5'b01001), .eq(BusWriteEnable));  // open: gt, lt
  or or_6 (or_6_out, and_1_out, and_2_out);
  // Probe on in_1

  // Notes on the sheet:
  //   offset: (word addressed)
  //   label: for j, jal (word addressed)
  //   PC + 4
  //   BRANCH
  //   jr/jalr
  //   register: for jr, jalr (byte addressed)
  //   any j*
  //   if register equality is right for branch type
  //   contents of rom_1 (hex, n*v repeats v):
  //   20080000 8c880000 8d480004 20880001 84080 3a8e822 1d2802 ac050000 804020 20a90004 2018ffff af090000
  //   21290004 2108ffff 1500000b 140f809 20500000 8000040 23bdfff0 ae1d0000 ae3d0004 ae5d0008 affd000c
  //   20900000 2208ffff 84880 a94820 8e290000 220502a 11400021 21040000 c000012 20510000 104042 84880
  //   a94820 8e490000 240502a 1140002a 21040000 c000012 20520000 2321020 20080005 208001a 4010 11000034
  //   20080003 208001a 4012 481020 8000037 2100018 4012 481020 104080 a84020 ac480000 8e1d0000 8e3d0004
  //   8e5d0008 8ffd000c 23bd0010 3e00008 8000040
  //   immediate
  //   label to jump to
  //   rs-data
  //   probe to help test the value in a wire
  //   MEM
  //   ALU
  //   PC + 4
  //   jal/jalr
  //   value from memory
  //   jal
  //   jalr
  //   checks ALU to see if its lw or sll
  //   value from ALU
  //   j
  //   jr
  //   what's going in
  //   storage location
  //   Checks if its sw
  //   whats coming out
endmodule

module MemoryController (
  input  WriteEnableFromBus,
  input  [25:0] AddressFromBus,
  input  [31:0] DataFromBus,
  input  [31:0] DataFromMem,
  output [31:0] DataToBus,
  output WriteToBus,
  output WriteEnableToMem,
  output [23:0] AddressToMem,
  output [31:0] DataToMem
);

  wire comparator_1_lt, not_1_out, not_2_out;

  Comparator #(.mode("unsigned"), .width(26)) comparator_1 (
    .a(AddressFromBus), .b(26'h3ffff00), .lt(comparator_1_lt));  // open: gt, eq
  Bit_Extender #(.in_width(26), .out_width(24)) bit_extender_1 (.in(AddressFromBus), .out(AddressToMem));
  not not_1 (not_1_out, WriteEnableFromBus);
  and and_1 (WriteToBus, not_1_out, comparator_1_lt);
  not not_2 (not_2_out, WriteToBus);
  and and_2 (WriteEnableToMem, not_2_out, comparator_1_lt);

  assign DataToBus = DataFromMem;
  assign DataToMem = DataFromBus;
endmodule

module KeyboardController (
  input  [31:0] DataFromBus,
  input  WriteEnableFromBus,
  input  [25:0] AddressFromBus,
  input  [6:0] KeyboardData,
  input  KeyboardStatus,
  output WriteToBus,
  output [31:0] DataToBus,
  output KeyboardRead
);

  wire and_2_out, and_3_out, and_4_out, comparator_1_eq, comparator_2_eq, multiplexer_1_out, not_1_out,
       not_2_out;
  wire [31:0] bit_extender_1_out, bit_extender_2_out;

  Comparator #(.width(26)) comparator_1 (.a(AddressFromBus), .b(26'h3ffffc4), .eq(comparator_1_eq));  // open: gt, lt
  Comparator #(.width(26)) comparator_2 (.a(AddressFromBus), .b(26'h3ffffc5), .eq(comparator_2_eq));  // open: gt, lt
  and and_1 (KeyboardRead, comparator_1_eq, WriteEnableFromBus);
  not not_1 (not_1_out, WriteEnableFromBus);
  not not_2 (not_2_out, WriteEnableFromBus);
  and and_2 (and_2_out, not_1_out, comparator_1_eq);
  and and_3 (and_3_out, comparator_1_eq, not_2_out);
  and and_4 (and_4_out, not_2_out, comparator_2_eq);
  Multiplexer multiplexer_1 (.in0(1'b0), .in1(KeyboardStatus), .out(multiplexer_1_out), .sel(and_3_out));
  or or_1 (WriteToBus, and_2_out, and_4_out);
  assign bit_extender_1_out = {{31{multiplexer_1_out}}, multiplexer_1_out};  // Bit_Extender bit_extender_1
  assign bit_extender_2_out = {{25{1'b0}}, KeyboardData};  // Bit_Extender bit_extender_2
  Multiplexer #(.width(32)) multiplexer_2 (
    .in0(bit_extender_1_out), .in1(bit_extender_2_out), .out(DataToBus), .sel(and_4_out));
endmodule

module RGBController (
  input  [25:0] AddressFromBus,
  input  [31:0] DataFromBus,
  input  WriteEnable,
  output [7:0] RGBX,
  output [7:0] RGBY,
  output [23:0] RGBColor,
  output RGBWrite
);

  wire and_1_out, and_2_out, and_3_out, clock_1_out, comparator_1_eq, comparator_2_eq, comparator_3_eq,
       comparator_4_eq;
  wire [7:0] bit_extender_1_out, bit_extender_2_out;
  wire [23:0] bit_extender_3_out;

  Comparator #(.width(26)) comparator_1 (.a(26'h3ffffc8), .b(AddressFromBus), .eq(comparator_1_eq));  // open: gt, lt
  and and_1 (and_1_out, comparator_1_eq, WriteEnable);
  Comparator #(.width(26)) comparator_2 (.a(AddressFromBus), .b(26'h3ffffc9), .eq(comparator_2_eq));  // open: gt, lt
  and and_2 (and_2_out, comparator_2_eq, WriteEnable);
  Comparator #(.width(26)) comparator_3 (.a(AddressFromBus), .b(26'h3ffffca), .eq(comparator_3_eq));  // open: gt, lt
  and and_3 (and_3_out, comparator_3_eq, WriteEnable);
  and and_4 (RGBWrite, WriteEnable, comparator_4_eq);
  Comparator #(.width(26)) comparator_4 (.a(AddressFromBus), .b(26'h3ffffcb), .eq(comparator_4_eq));  // open: gt, lt
  Register x_coords (.D(bit_extender_1_out), .en(and_1_out), .clk(clock_1_out), .Q(RGBX));  // open: clr
  Bit_Extender #(.in_width(32), .out_width(8)) bit_extender_1 (.in(DataFromBus), .out(bit_extender_1_out));
  Clock clock_1 (.out(clock_1_out));
  Register y_coords (.D(bit_extender_2_out), .en(and_2_out), .clk(clock_1_out), .Q(RGBY));  // open: clr
  Bit_Extender #(.in_width(32), .out_width(8)) bit_extender_2 (.in(DataFromBus), .out(bit_extender_2_out));
  Register #(.width(24)) RGB (.D(bit_extender_3_out), .en(and_3_out), .clk(clock_1_out), .Q(RGBColor));  // open: clr
  Bit_Extender #(.in_width(32), .out_width(24)) bit_extender_3 (.in(DataFromBus), .out(bit_extender_3_out));
endmodule

module TerminalController (
  input  WriteEnableFromBus,
  input  [25:0] AddressFromBus,
  input  [31:0] DataFromBus,
  output [6:0] DataToTerminal,
  output WriteToTerminal
);

  wire and_1_out, comparator_1_eq;
  wire [6:0] bit_extender_1_out;

  Comparator #(.mode("unsigned"), .width(26)) comparator_1 (
    .a(AddressFromBus), .b(26'h3ffffc0), .eq(comparator_1_eq));  // open: gt, lt
  and and_1 (and_1_out, WriteEnableFromBus, comparator_1_eq);
  Bit_Extender #(.in_width(32), .out_width(7)) bit_extender_1 (.in(DataFromBus), .out(bit_extender_1_out));
  Multiplexer #(.width(7)) multiplexer_1 (
    .in0({7{1'b0}}), .in1(bit_extender_1_out), .out(DataToTerminal), .sel(and_1_out));

  assign WriteToTerminal = WriteEnableFromBus;
endmodule

module NEW_regfile (
  input  [4:0] RS_Select,
  input  [4:0] RT_Select,
  input  Write_Enable,
  input  [4:0] RD_Select,
  input  [31:0] RD_Data,
  output [31:0] RS_Data,
  output [31:0] RT_Data
);

  wire Clock1_out, demultiplexer_1_out1, demultiplexer_1_out2, demultiplexer_1_out3, demultiplexer_1_out4,
       demultiplexer_1_out5, demultiplexer_1_out6, demultiplexer_1_out7, demultiplexer_1_out8,
       demultiplexer_1_out9, demultiplexer_1_out10, demultiplexer_1_out11, demultiplexer_1_out12,
       demultiplexer_1_out13, demultiplexer_1_out14, demultiplexer_1_out15, demultiplexer_1_out16,
       demultiplexer_1_out17, demultiplexer_1_out18, demultiplexer_1_out19, demultiplexer_1_out20,
       demultiplexer_1_out21, demultiplexer_1_out22, demultiplexer_1_out23, demultiplexer_1_out24,
       demultiplexer_1_out25, demultiplexer_1_out26, demultiplexer_1_out27, demultiplexer_1_out28,
       demultiplexer_1_out29, demultiplexer_1_out30, demultiplexer_1_out31;
  wire [31:0] Reg1_q, Reg2_q, Reg3_q, Reg4_q, Reg5_q, Reg6_q, Reg7_q, Reg8_q, Reg9_q, Reg10_q, Reg11_q,
       Reg12_q, Reg13_q, Reg14_q, Reg15_q, Reg16_q, Reg17_q, Reg18_q, Reg19_q, Reg20_q, Reg21_q, Reg22_q,
       Reg23_q, Reg24_q, Reg25_q, Reg26_q, Reg27_q, Reg28_q, Reg29_q, Reg30_q, Reg31_q;

  Clock Clock1 (.out(Clock1_out));
  Demultiplexer #(.select(5)) demultiplexer_1 (
    .out1(demultiplexer_1_out1), .out2(demultiplexer_1_out2), .out3(demultiplexer_1_out3),
    .out4(demultiplexer_1_out4), .out5(demultiplexer_1_out5), .out6(demultiplexer_1_out6),
    .out7(demultiplexer_1_out7), .out8(demultiplexer_1_out8), .out9(demultiplexer_1_out9),
    .out10(demultiplexer_1_out10), .out11(demultiplexer_1_out11), .out12(demultiplexer_1_out12),
    .out13(demultiplexer_1_out13), .out14(demultiplexer_1_out14), .out15(demultiplexer_1_out15),
    .out16(demultiplexer_1_out16), .out17(demultiplexer_1_out17), .out18(demultiplexer_1_out18),
    .out19(demultiplexer_1_out19), .out20(demultiplexer_1_out20), .out21(demultiplexer_1_out21),
    .out22(demultiplexer_1_out22), .out23(demultiplexer_1_out23), .out24(demultiplexer_1_out24),
    .out25(demultiplexer_1_out25), .out26(demultiplexer_1_out26), .out27(demultiplexer_1_out27),
    .out28(demultiplexer_1_out28), .out29(demultiplexer_1_out29), .out30(demultiplexer_1_out30),
    .out31(demultiplexer_1_out31), .in(Write_Enable), .sel(RD_Select));  // open: out0
  Register #(.width(32)) Reg1 (.D(RD_Data), .en(demultiplexer_1_out1), .clk(Clock1_out), .Q(Reg1_q));  // open: clr
  Register #(.width(32)) Reg2 (.D(RD_Data), .en(demultiplexer_1_out2), .clk(Clock1_out), .Q(Reg2_q));  // open: clr
  Register #(.width(32)) Reg3 (.D(RD_Data), .en(demultiplexer_1_out3), .clk(Clock1_out), .Q(Reg3_q));  // open: clr
  Register #(.width(32)) Reg4 (.D(RD_Data), .en(demultiplexer_1_out4), .clk(Clock1_out), .Q(Reg4_q));  // open: clr
  Register #(.width(32)) Reg5 (.D(RD_Data), .en(demultiplexer_1_out5), .clk(Clock1_out), .Q(Reg5_q));  // open: clr
  Register #(.width(32)) Reg6 (.D(RD_Data), .en(demultiplexer_1_out6), .clk(Clock1_out), .Q(Reg6_q));  // open: clr
  Register #(.width(32)) Reg7 (.D(RD_Data), .en(demultiplexer_1_out7), .clk(Clock1_out), .Q(Reg7_q));  // open: clr
  Register #(.width(32)) Reg8 (.D(RD_Data), .en(demultiplexer_1_out8), .clk(Clock1_out), .Q(Reg8_q));  // open: clr
  Register #(.width(32)) Reg9 (.D(RD_Data), .en(demultiplexer_1_out9), .clk(Clock1_out), .Q(Reg9_q));  // open: clr
  Register #(.width(32)) Reg10 (.D(RD_Data), .en(demultiplexer_1_out10), .clk(Clock1_out), .Q(Reg10_q));  // open: clr
  Register #(.width(32)) Reg11 (.D(RD_Data), .en(demultiplexer_1_out11), .clk(Clock1_out), .Q(Reg11_q));  // open: clr
  Register #(.width(32)) Reg12 (.D(RD_Data), .en(demultiplexer_1_out12), .clk(Clock1_out), .Q(Reg12_q));  // open: clr
  Register #(.width(32)) Reg13 (.D(RD_Data), .en(demultiplexer_1_out13), .clk(Clock1_out), .Q(Reg13_q));  // open: clr
  Register #(.width(32)) Reg14 (.D(RD_Data), .en(demultiplexer_1_out14), .clk(Clock1_out), .Q(Reg14_q));  // open: clr
  Register #(.width(32)) Reg15 (.D(RD_Data), .en(demultiplexer_1_out15), .clk(Clock1_out), .Q(Reg15_q));  // open: clr
  Register #(.width(32)) Reg16 (.D(RD_Data), .en(demultiplexer_1_out16), .clk(Clock1_out), .Q(Reg16_q));  // open: clr
  // Probe on Reg16_q
  Register #(.width(32)) Reg17 (.D(RD_Data), .en(demultiplexer_1_out17), .clk(Clock1_out), .Q(Reg17_q));  // open: clr
  Register #(.width(32)) Reg18 (.D(RD_Data), .en(demultiplexer_1_out18), .clk(Clock1_out), .Q(Reg18_q));  // open: clr
  Register #(.width(32)) Reg19 (.D(RD_Data), .en(demultiplexer_1_out19), .clk(Clock1_out), .Q(Reg19_q));  // open: clr
  Register #(.width(32)) Reg20 (.D(RD_Data), .en(demultiplexer_1_out20), .clk(Clock1_out), .Q(Reg20_q));  // open: clr
  Register #(.width(32)) Reg21 (.D(RD_Data), .en(demultiplexer_1_out21), .clk(Clock1_out), .Q(Reg21_q));  // open: clr
  Register #(.width(32)) Reg22 (.D(RD_Data), .en(demultiplexer_1_out22), .clk(Clock1_out), .Q(Reg22_q));  // open: clr
  Register #(.width(32)) Reg23 (.D(RD_Data), .en(demultiplexer_1_out23), .clk(Clock1_out), .Q(Reg23_q));  // open: clr
  Register #(.width(32)) Reg24 (.D(RD_Data), .en(demultiplexer_1_out24), .clk(Clock1_out), .Q(Reg24_q));  // open: clr
  Register #(.width(32)) Reg25 (.D(RD_Data), .en(demultiplexer_1_out25), .clk(Clock1_out), .Q(Reg25_q));  // open: clr
  Register #(.width(32)) Reg26 (.D(RD_Data), .en(demultiplexer_1_out26), .clk(Clock1_out), .Q(Reg26_q));  // open: clr
  Register #(.width(32)) Reg27 (.D(RD_Data), .en(demultiplexer_1_out27), .clk(Clock1_out), .Q(Reg27_q));  // open: clr
  Register #(.width(32)) Reg28 (.D(RD_Data), .en(demultiplexer_1_out28), .clk(Clock1_out), .Q(Reg28_q));  // open: clr
  Register #(.width(32)) Reg29 (.D(RD_Data), .en(demultiplexer_1_out29), .clk(Clock1_out), .Q(Reg29_q));  // open: clr
  Register #(.width(32)) Reg30 (.D(RD_Data), .en(demultiplexer_1_out30), .clk(Clock1_out), .Q(Reg30_q));  // open: clr
  Register #(.width(32)) Reg31 (.D(RD_Data), .en(demultiplexer_1_out31), .clk(Clock1_out), .Q(Reg31_q));  // open: clr
  Multiplexer #(.select(5), .width(32)) multiplexer_1 (
    .in0({32{1'b0}}), .in1(Reg1_q), .in2(Reg2_q), .in3(Reg3_q), .in4(Reg4_q), .in5(Reg5_q), .in6(Reg6_q),
    .in7(Reg7_q), .in8(Reg8_q), .in9(Reg9_q), .in10(Reg10_q), .in11(Reg11_q), .in12(Reg12_q), .in13(Reg13_q),
    .in14(Reg14_q), .in15(Reg15_q), .in16(Reg16_q), .in17(Reg17_q), .in18(Reg18_q), .in19(Reg19_q),
    .in20(Reg20_q), .in21(Reg21_q), .in22(Reg22_q), .in23(Reg23_q), .in24(Reg24_q), .in25(Reg25_q),
    .in26(Reg26_q), .in27(Reg27_q), .in28(Reg28_q), .in29(Reg29_q), .in30(Reg30_q), .in31(Reg31_q),
    .out(RS_Data), .sel(RS_Select));
  Multiplexer #(.select(5), .width(32)) multiplexer_2 (
    .in0({32{1'b0}}), .in1(Reg1_q), .in2(Reg2_q), .in3(Reg3_q), .in4(Reg4_q), .in5(Reg5_q), .in6(Reg6_q),
    .in7(Reg7_q), .in8(Reg8_q), .in9(Reg9_q), .in10(Reg10_q), .in11(Reg11_q), .in12(Reg12_q), .in13(Reg13_q),
    .in14(Reg14_q), .in15(Reg15_q), .in16(Reg16_q), .in17(Reg17_q), .in18(Reg18_q), .in19(Reg19_q),
    .in20(Reg20_q), .in21(Reg21_q), .in22(Reg22_q), .in23(Reg23_q), .in24(Reg24_q), .in25(Reg25_q),
    .in26(Reg26_q), .in27(Reg27_q), .in28(Reg28_q), .in29(Reg29_q), .in30(Reg30_q), .in31(Reg31_q),
    .out(RT_Data), .sel(RT_Select));

  // Notes on the sheet:
  //   Brett Barnes & Henry Groves
endmodule

module NEW_Control (
  input  [31:0] Inst,
  output [31:0] imm,
  output imm_sel,
  output we_regfile,
  output [4:0] rs_select,
  output [4:0] rt_select,
  output [4:0] rd_select,
  output [4:0] ALU_operation,
  output ALUvMEMselect,
  output we_mem,
  output [4:0] Shamt
);

  wire and_1_out, and_2_out, and_3_out, and_4_out, and_6_out, and_7_out, comparator_1_eq, comparator_2_eq,
       comparator_3_eq, comparator_4_eq, comparator_5_eq, comparator_6_eq, comparator_7_eq, comparator_8_eq,
       comparator_9_eq, comparator_12_eq, comparator_13_eq, comparator_14_eq, comparator_15_eq,
       comparator_16_eq, comparator_17_eq, comparator_18_eq, comparator_19_eq, comparator_20_eq,
       comparator_21_eq, nor_1_out, not_1_out, not_2_out, not_3_out, not_4_out, not_5_out, not_6_out,
       not_7_out, not_8_out, not_9_out, not_10_out, or_1_out, or_2_out, or_3_out, or_4_out, or_5_out;
  wire [4:0] demultiplexer_1_out0, demultiplexer_1_out1, demultiplexer_2_out0, demultiplexer_2_out1,
       multiplexer_1_out, multiplexer_2_out, multiplexer_3_out, multiplexer_4_out, multiplexer_5_out,
       multiplexer_7_out, multiplexer_10_out, undriven, undriven_2;

  Clock clock_1 ();  // open: out
  Comparator #(.width(6)) comparator_1 (.a(6'b101011), .b(Inst[31:26]), .eq(comparator_1_eq));  // open: gt, lt
  Multiplexer #(.select(5), .width(5)) multiplexer_1 (
    .in0(5'b00101), .in1(undriven), .in2(5'b00110), .in4(5'b10000), .in5(5'b10011), .in6(undriven_2),
    .in7(undriven_2), .in8(5'b00100), .in10({5{1'b1}}), .in12(5'b00010), .in13(undriven_2), .in14(5'b00011),
    .in15(undriven_2), .in16({5{1'b0}}), .in17(undriven_2), .in18(5'b00001), .in19(undriven_2),
    .in20(undriven_2), .in21(undriven_2), .in22(5'b00111), .in23(undriven_2), .in24(undriven_2),
    .in25(undriven_2), .in26(undriven_2), .in27(undriven_2), .in28(undriven_2), .in29(undriven_2),
    .in30(undriven_2), .in31(undriven_2), .out(multiplexer_1_out), .sel({Inst[5:3], Inst[1:0]}));  // open: in3, in9, in11
  Multiplexer #(.width(5)) multiplexer_2 (
    .in0(multiplexer_1_out), .in1(5'b10100), .out(multiplexer_2_out), .sel(Inst[2]));
  not not_1 (not_1_out, comparator_1_eq);
  not not_2 (not_2_out, comparator_2_eq);
  Comparator #(.mode("unsigned"), .width(6)) comparator_2 (
    .a({6{1'b0}}), .b(Inst[31:26]), .eq(comparator_2_eq));  // open: gt, lt
  Multiplexer #(.width(5)) multiplexer_3 (.in0(5'b10001), .in1(5'b01000), .out(multiplexer_3_out), .sel(Inst[31]));
  Comparator #(.width(6)) comparator_3 (.a(6'b000011), .b(Inst[31:26]), .eq(comparator_3_eq));  // open: gt, lt
  Comparator #(.width(6)) comparator_4 (.a(Inst[31:26]), .b(6'b100011), .eq(comparator_4_eq));  // open: gt, lt
  Demultiplexer #(.width(5)) demultiplexer_1 (
    .out0(demultiplexer_1_out0), .out1(demultiplexer_1_out1), .in(Inst[20:16]), .sel(and_1_out));
  and and_1 (and_1_out, not_2_out, not_8_out);
  Demultiplexer #(.width(5)) demultiplexer_2 (
    .out0(demultiplexer_2_out0), .out1(demultiplexer_2_out1), .in(Inst[15:11]), .sel(not_2_out));
  Multiplexer #(.select(4), .width(5)) multiplexer_4 (
    .in2(5'b01111), .in3(multiplexer_3_out), .in4(5'b01010), .in5(5'b01011), .in8({5{1'b0}}),
    .in11(5'b01001), .out(multiplexer_4_out));  // open: in0, in1, in6, in7, in9, in10, in12, in13, in14, in15, sel
  not not_3 (not_3_out, not_2_out);
  Multiplexer #(.width(5)) multiplexer_5 (
    .in0(demultiplexer_1_out1), .in1(demultiplexer_2_out0), .out(multiplexer_5_out), .sel(not_3_out));
  Comparator #(.mode("unsigned"), .width(6)) comparator_5 (
    .a(6'b011010), .b(Inst[5:0]), .eq(comparator_5_eq));  // open: gt, lt
  Comparator #(.mode("unsigned"), .width(6)) comparator_6 (
    .a(Inst[5:0]), .b(6'b011000), .eq(comparator_6_eq));  // open: gt, lt
  Comparator #(.width(6)) comparator_7 (.a(Inst[31:26]), .b(6'b000100), .eq(comparator_7_eq));  // open: gt, lt
  Comparator #(.width(6)) comparator_8 (.a(Inst[31:26]), .b(6'b000101), .eq(comparator_8_eq));  // open: gt, lt
  not not_4 (not_4_out, not_2_out);
  Multiplexer #(.width(5)) multiplexer_6 (
    .in0(multiplexer_4_out), .in1(multiplexer_2_out), .out(ALU_operation), .sel(not_4_out));
  not not_5 (not_5_out, imm_sel);
  assign imm = {{16{demultiplexer_2_out1[4]}}, {demultiplexer_2_out1, Inst[10:0]}};  // Bit_Extender bit_extender_1
  and and_2 (and_2_out, not_5_out, comparator_5_eq);
  and and_3 (and_3_out, not_5_out, comparator_6_eq);
  not not_6 (not_6_out, comparator_7_eq);
  and and_4 (and_4_out, not_2_out, not_7_out);
  not not_7 (not_7_out, comparator_8_eq);
  Comparator #(.width(6)) comparator_9 (.a(Inst[31:26]), .b(6'b000011), .eq(comparator_9_eq));  // open: gt, lt
  Comparator #(.width(6)) comparator_10 (.a(Inst[31:26]), .b(6'b100011), .eq(ALUvMEMselect));  // open: gt, lt
  Comparator #(.width(6)) comparator_11 (.a(Inst[31:26]), .b(6'b101011), .eq(we_mem));  // open: gt, lt
  nor nor_1 (nor_1_out, and_2_out, and_3_out);
  or or_1 (or_1_out, comparator_7_eq, comparator_8_eq);
  not not_8 (not_8_out, or_1_out);
  and and_5 (imm_sel, not_6_out, and_4_out);
  and and_6 (and_6_out, nor_1_out, not_8_out);
  not not_9 (not_9_out, not_1_out);
  Multiplexer #(.width(5)) multiplexer_7 (
    .in0(multiplexer_5_out), .in1({5{1'b1}}), .out(multiplexer_7_out), .sel(comparator_9_eq));
  and and_7 (and_7_out, not_1_out, and_6_out);
  Multiplexer #(.width(5)) multiplexer_8 (.in0(Inst[25:21]), .in1(multiplexer_5_out), .out(rs_select), .sel(not_9_out));
  Multiplexer #(.width(5)) multiplexer_9 (
    .in0(demultiplexer_1_out0), .in1(multiplexer_10_out), .out(rt_select), .sel(not_10_out));
  Multiplexer #(.width(5)) multiplexer_10 (
    .in0(multiplexer_5_out), .in1(Inst[25:21]), .out(multiplexer_10_out), .sel(not_9_out));
  Multiplexer #(.width(5)) multiplexer_11 (
    .in0(multiplexer_7_out), .in1(Inst[25:21]), .out(rd_select), .sel(comparator_4_eq));
  Multiplexer multiplexer_12 (.in0(and_7_out), .in1(not_10_out), .out(we_regfile), .sel(or_2_out));
  Comparator #(.width(5)) comparator_12 (.a(5'b00101), .b(ALU_operation), .eq(comparator_12_eq));  // open: gt, lt
  Comparator #(.width(5)) comparator_13 (.a(ALU_operation), .b(5'b00110), .eq(comparator_13_eq));  // open: gt, lt
  Comparator #(.width(5)) comparator_14 (.a(ALU_operation), .b(5'b01010), .eq(comparator_14_eq));  // open: gt, lt
  Comparator #(.width(5)) comparator_15 (.a(ALU_operation), .b(5'b01011), .eq(comparator_15_eq));  // open: gt, lt
  Comparator #(.width(5)) comparator_16 (.a(ALU_operation), .b(5'b00011), .eq(comparator_16_eq));  // open: gt, lt
  Comparator #(.width(5)) comparator_17 (.a(ALU_operation), .b(5'b00010), .eq(comparator_17_eq));  // open: gt, lt
  Comparator #(.width(5)) comparator_18 (.a(ALU_operation), .b({5{1'b0}}), .eq(comparator_18_eq));  // open: gt, lt
  Comparator #(.width(5)) comparator_19 (.a(ALU_operation), .b(5'b00001), .eq(comparator_19_eq));  // open: gt, lt
  Comparator #(.width(5)) comparator_20 (.a(ALU_operation), .b(5'b00111), .eq(comparator_20_eq));  // open: gt, lt
  or or_2 (or_2_out, comparator_3_eq, comparator_21_eq);
  Comparator #(.width(5)) comparator_21 (.a(5'b10011), .b(ALU_operation), .eq(comparator_21_eq));  // open: gt, lt
  or or_3 (or_3_out, comparator_12_eq, comparator_13_eq, comparator_14_eq, or_4_out);
  or or_4 (or_4_out, comparator_15_eq, comparator_16_eq, comparator_17_eq, or_5_out);
  or or_5 (or_5_out, comparator_18_eq, comparator_20_eq, comparator_19_eq);
  not not_10 (not_10_out, or_3_out);

  assign Shamt = Inst[10:6];

  // Notes on the sheet:
  //   op code
  //   func code
  //   to check if opcode is for sw, disable write for reg
  //   rs
  //   if lw, rs -> rd
  //   div & mult
  //   check if its branch to avoid incorrect imm sel
  //   rs
  //   rt
  //   rt
  //   rd
  //   rd
  //   rs
  //   rt
  //   rt
  //   rd
  //   rd
  //   rd
  //   rd
  //   rs
  //   on if !sw
  //   if it is sw, flip rs & rt
  //   rs
  //   rd
  //   rd
  //   if lw, rs -> rd
  //   Note: More outputs will be needed
endmodule

module NEW_ALU (
  input  [31:0] OP1,
  input  [31:0] OP2,
  input  [4:0] shift,
  input  [4:0] ALU_CODE,
  output [31:0] Res,
  output equal
);

  wire clock_2_out, comparator_1_lt, comparator_2_eq, comparator_3_eq, or_1_out;
  wire [31:0] adder_1_out, adder_2_out, divider_1_out, divider_1_rem, HI_q, LO_q, multiplexer_1_out,
       multiplexer_2_out, multiplexer_3_out, multiplier_1_cout, multiplier_1_out, shifter_1_out,
       shifter_2_out, subtractor_1_out;

  Clock clock_1 ();  // open: out
  Adder #(.width(32)) adder_1 (.a(OP1), .b(OP2), .out(adder_1_out));  // open: cin, cout
  Subtractor #(.width(32)) subtractor_1 (.a(OP1), .b(OP2), .out(subtractor_1_out));  // open: bin, bout
  Multiplier #(.width(32)) multiplier_1 (
    .a(OP1), .b(OP2), .out(multiplier_1_out), .cout(multiplier_1_cout));  // open: cin
  Divider #(.width(32)) divider_1 (.a(OP1), .b(OP2), .out(divider_1_out), .rem(divider_1_rem));  // open: upper
  Shifter #(.width(32)) shifter_1 (.in(OP1), .\dist (shift), .out(shifter_1_out));
  Shifter #(.shift("lr"), .width(32)) shifter_2 (.in(OP1), .\dist (shift), .out(shifter_2_out));
  Comparator #(.mode("unsigned"), .width(32)) comparator_1 (
    .a(OP1), .b(OP2), .eq(equal), .lt(comparator_1_lt));  // open: gt
  Adder #(.width(32)) adder_2 (.a(OP1), .b(OP2), .out(adder_2_out));  // open: cin, cout
  Comparator #(.mode("unsigned"), .width(5)) comparator_2 (
    .a(ALU_CODE), .b(5'b00010), .eq(comparator_2_eq));  // open: gt, lt
  Comparator #(.mode("unsigned"), .width(5)) comparator_3 (
    .a(ALU_CODE), .b(5'b00011), .eq(comparator_3_eq));  // open: gt, lt
  Multiplexer #(.select(5), .width(32)) multiplexer_1 (
    .in2(multiplier_1_out), .in3(divider_1_out), .out(multiplexer_1_out), .sel(ALU_CODE));  // open: in0, in1, in4, in5, in6, in7, in8, in9, in10, in11, in12, in13, in14, in15, in16, in17, in18, in19, in20, in21, in22, in23, in24, in25, in26, in27, in28, in29, in30, in31
  Clock clock_2 (.out(clock_2_out));
  Multiplexer #(.select(5), .width(32)) multiplexer_2 (
    .in2(multiplier_1_cout), .in3(divider_1_rem), .out(multiplexer_2_out), .sel(ALU_CODE));  // open: in0, in1, in4, in5, in6, in7, in8, in9, in10, in11, in12, in13, in14, in15, in16, in17, in18, in19, in20, in21, in22, in23, in24, in25, in26, in27, in28, in29, in30, in31
  or or_1 (or_1_out, comparator_2_eq, comparator_3_eq);
  Register #(.width(32)) LO (.D(multiplexer_1_out), .en(or_1_out), .clk(clock_2_out), .Q(LO_q));  // open: clr
  Register #(.width(32)) HI (.D(multiplexer_2_out), .en(or_1_out), .clk(clock_2_out), .Q(HI_q));  // open: clr
  Multiplexer #(.width(32)) multiplexer_3 (
    .in0({32{1'b0}}), .in1(32'h1), .out(multiplexer_3_out), .sel(comparator_1_lt));
  Multiplexer #(.select(5), .width(32)) multiplexer_4 (
    .in0(adder_1_out), .in1(subtractor_1_out), .in2({32{1'b0}}), .in3({32{1'b0}}), .in4(HI_q),
    .in5(shifter_1_out), .in6(shifter_2_out), .in7(multiplexer_3_out), .in8(adder_2_out), .in9(adder_2_out),
    .in10({32{1'b0}}), .in11({32{1'b0}}), .in12(OP2), .in13(OP1), .in14(OP2), .in15(OP1), .in16(OP1),
    .in31(LO_q), .out(Res), .sel(ALU_CODE));  // open: in17, in18, in19, in20, in21, in22, in23, in24, in25, in26, in27, in28, in29, in30

  // Notes on the sheet:
  //   mflo/mfhi
  //   mflo/mfhi
  //   add
  //   sub
  //   sll
  //   srl
  //   slt
  //   sw/lw
  //   jr/jalr/syscall
  //   mult/div
  //   beq/bne
  //   j/jal
endmodule
